// Logisim project CIRCUITO1.circ as structural Verilog: 1 circuit, main circuit main
module main (
  input  a,
  input  b,
  input  c_in,
  output c_out,
  output s
);

  wire and_1_out, and_2_out, or_1_out;

  and and_1 (and_1_out, a, b);
  or or_1 (or_1_out, a, b);
  or or_2 (c_out, and_1_out, and_2_out);
  and and_2 (and_2_out, or_1_out, c_in);
  xor xor_1 (s, a, b, c_in);
endmodule
