// Logisim project PD1_Pérez_Fraguela_Eduardo.circ as structural Verilog: 1 circuit, main circuit main
module main (
  input  [3:0] A,
  input  [3:0] B
);

  wire comparator_1_gt, comparator_2_gt, or_1_out;
  wire [4:0] _2_B_4, A_3, multiplexer_1_out, not_1_out;

  // Probe on B
  // Probe on {{2{A[3]}}, A[2:0]}
  // Probe on {B, 1'b0}
  // Probe on {B, 1'b0}
  Comparator #(.width(5)) comparator_1 (.a({{2{A[3]}}, A[2:0]}), .b(5'b00011), .gt(comparator_1_gt));  // open: eq, lt
  Comparator #(.width(4)) comparator_2 (.a(4'b0100), .b(B), .gt(comparator_2_gt));  // open: eq, lt
  or or_1 (or_1_out, comparator_1_gt, comparator_2_gt);
  Adder #(.width(5)) adder_1 (.a({{2{A[3]}}, A[2:0]}), .b(5'b00011), .out(A_3));  // open: cin, cout
  assign not_1_out = ~5'b00100;  // NOT_Gate not_1, 5 bits wide
  // Probe on A_3
  // Probe on A_3
  // Probe on _2_B_4
  // Probe on _2_B_4
  Adder #(.width(5)) adder_2 (.a(not_1_out), .b({B, 1'b0}), .out(_2_B_4), .cin(1'b1));  // open: cout
  Multiplexer #(.width(5), .disabled(0), .enable("false")) multiplexer_1 (
    .in0(_2_B_4), .in1(A_3), .out(multiplexer_1_out), .sel(or_1_out));
  // Probe on multiplexer_1_out
  // Probe on multiplexer_1_out

  // Other names for the same wires on the sheet: _2_B[4:1] = B; A_t[4:0] = {{2{A[3]}}, A[2:0]}

  // Notes on the sheet:
  //   A
  //   2*B
  //   IF (A > 3 OR B < 4)
  //   Y = A+3
  //   ELSE
  //   Y = 2*B-4
  //   A+3
  //   2*B-4
  //   Y
endmodule
