// Logisim project PD2.circ as structural Verilog: 1 circuit, main circuit main
module main (
  input  [3:0] in_1,
  input  in_2
);

  wire CICLO7, CLK, comparator_1_eq, comparator_3_gt, INICIO, or_1_out;
  wire [2:0] SOLUCION, Y;
  wire [3:0] ANTERIOR, CONT;

  Clock clock_1 (.out(CLK));
  // Probe on in_1
  // Probe on ANTERIOR
  Comparator #(.width(4), .mode("unsigned")) comparator_1 (
    .a(CONT), .b(4'b1000), .eq(comparator_1_eq));  // open: gt, lt
  Comparator #(.width(4), .mode("unsigned")) comparator_2 (.a(4'b0000), .b(CONT), .eq(INICIO));  // open: gt, lt
  // Probe on ANTERIOR
  Register #(.width(4)) register_1 (.D(in_1), .Q(ANTERIOR), .clk(CLK), .clr(in_2));  // open: en
  Multiplexer #(.width(3), .disabled(0), .enable("false")) multiplexer_1 (
    .in1(SOLUCION), .out(Y), .sel(comparator_1_eq));  // open: in0
  Comparator #(.width(4), .mode("unsigned")) comparator_3 (
    .a({ANTERIOR[3], in_1[2:0]}), .b({in_1[3], ANTERIOR[2:0]}), .gt(comparator_3_gt));  // open: eq, lt
  or or_1 (or_1_out, comparator_3_gt, INICIO, CICLO7);
  // Probe on Y
  Counter #(.width(4), .max('h8)) counter_1 (.Q(CONT), .clk(CLK), .clr(in_2));  // open: load, D, count, carry
  Counter #(.width(3), .max('h7)) counter_2 (
    .count(or_1_out), .Q(SOLUCION), .clk(CLK), .clr(in_2));  // open: load, D, carry
  Comparator #(.width(4), .mode("unsigned")) comparator_4 (.a(4'b0111), .b(CONT), .eq(CICLO7));  // open: gt, lt

  // Other names for the same wires on the sheet: X[3:0] = in_1; RESET = in_2
endmodule
