// Logisim project PD2_Pérez_Fraguela_Eduardo.circ as structural Verilog: 1 circuit, main circuit main
module main (
  input  [3:0] in_1,
  input  in_2
);

  wire ACARREO, and_2_out, CLEAR, CLK, comparator_1_gt, comparator_2_gt, Count_5_X_A, ENABLE, or_1_out,
       or_2_out, START;
  wire [2:0] Y;
  wire [3:0] A, CONT;

  Clock clock_1 (.out(CLK));
  // Probe on 4'b0101
  // Probe on in_1
  // Probe on A
  // Probe on in_1
  // Probe on A
  Register #(.width(4)) register_1 (.D(in_1), .en(ENABLE), .Q(A), .clk(CLK), .clr(in_2));
  Comparator #(.width(4), .mode("unsigned")) comparator_1 (
    .a({in_1[3], 3'b101}), .b({1'b0, in_1[2:0]}), .gt(comparator_1_gt));  // open: eq, lt
  Comparator #(.width(4), .mode("unsigned")) comparator_2 (
    .a({A[3], in_1[2:0]}), .b({in_1[3], A[2:0]}), .gt(comparator_2_gt));  // open: eq, lt
  and and_1 (Count_5_X_A, comparator_1_gt, START, comparator_2_gt);
  or or_1 (or_1_out, CONT[0], CONT[1], CONT[2], CONT[3]);
  Counter #(.width(3), .max('h7)) counter_1 (.Q(Y), .clk(and_2_out), .clr(in_2));  // open: load, D, count, carry
  and and_2 (and_2_out, Count_5_X_A, CLK);
  // Probe on or_1_out
  nor nor_1 (ENABLE, or_1_out, 1'b0);
  Counter #(.width(4), .max('h7)) counter_2 (
    .Q(CONT), .carry(ACARREO), .clk(CLK), .clr(or_2_out));  // open: load, D, count
  or or_2 (or_2_out, in_2, CLEAR);
  // Probe on ENABLE
  // Probe on Y
  Comparator #(.width(4), .mode("unsigned")) comparator_3 (.a(CONT), .b(4'b0111), .eq(CLEAR));  // open: gt, lt
  Comparator #(.width(4), .mode("unsigned")) comparator_4 (.a(CONT), .b(4'b0000), .gt(START));  // open: eq, lt

  // Other names for the same wires on the sheet: X[3:0] = in_1; RESET = in_2

  // Notes on the sheet:
  //   Variables
  //   Deseña e implementa usando o programa LogiSim un circuíto secuencial que reciba por
  //   unha entrada X (de 4 bits en complemento a 2) secuencias de 7 valores (un por ciclo) e
  //   conte cantas veces se cumple que 5 > X > A, sendo A o valor recibido pola entrada X no
  //   primeiro ciclo da secuencia. No oitavo ciclo mostrarase o valor da conta pola saída Y do
  //   circuíto (de 3 bits en binario puro) e non se usará o valor da entrada X.
  //   Eduardo Pérez Fraguela, Grupo 3.4
endmodule
