// Logisim project PRUEBA.circ as structural Verilog: 1 circuit, main circuit main
module main (
  input  in_1,
  input  [7:0] in_2,
  input  in_3,
  input  [7:0] in_4
);

  wire comparator_1_eq, comparator_1_gt, comparator_1_lt;
  wire [7:0] A, adder_1_out, B;

  D_Flip_Flop d_ff_1 (.clk(in_1), .D(in_2[7]), .Q(A[7]));  // open: Qn, preset, en, reset
  D_Flip_Flop d_ff_2 (.clk(in_1), .D(in_2[6]), .Q(A[6]));  // open: Qn, preset, en, reset
  Adder adder_1 (.a(A), .b(B), .out(adder_1_out));  // open: cin, cout
  Comparator #(.mode("unsigned")) comparator_1 (
    .a(A), .b(B), .gt(comparator_1_gt), .eq(comparator_1_eq), .lt(comparator_1_lt));
  D_Flip_Flop d_ff_3 (.clk(in_1), .D(in_2[5]), .Q(A[5]));  // open: Qn, preset, en, reset
  // Probe on adder_1_out
  // Probe on comparator_1_gt
  // Probe on comparator_1_eq
  // Probe on comparator_1_lt
  D_Flip_Flop d_ff_4 (.clk(in_1), .D(in_2[4]), .Q(A[4]));  // open: Qn, preset, en, reset
  D_Flip_Flop d_ff_5 (.clk(in_1), .D(in_2[3]), .Q(A[3]));  // open: Qn, preset, en, reset
  D_Flip_Flop d_ff_6 (.clk(in_1), .D(in_2[2]), .Q(A[2]));  // open: Qn, preset, en, reset
  D_Flip_Flop d_ff_7 (.clk(in_3), .D(in_4[7]), .Q(B[7]));  // open: Qn, preset, en, reset
  D_Flip_Flop d_ff_8 (.clk(in_1), .D(in_2[1]), .Q(A[1]));  // open: Qn, preset, en, reset
  D_Flip_Flop d_ff_9 (.clk(in_3), .D(in_4[6]), .Q(B[6]));  // open: Qn, preset, en, reset
  // Probe on A
  D_Flip_Flop d_ff_10 (.clk(in_1), .D(in_2[0]), .Q(A[0]));  // open: Qn, preset, en, reset
  D_Flip_Flop d_ff_11 (.clk(in_3), .D(in_4[5]), .Q(B[5]));  // open: Qn, preset, en, reset
  D_Flip_Flop d_ff_12 (.clk(in_3), .D(in_4[4]), .Q(B[4]));  // open: Qn, preset, en, reset
  D_Flip_Flop d_ff_13 (.clk(in_3), .D(in_4[3]), .Q(B[3]));  // open: Qn, preset, en, reset
  D_Flip_Flop d_ff_14 (.clk(in_3), .D(in_4[2]), .Q(B[2]));  // open: Qn, preset, en, reset
  D_Flip_Flop d_ff_15 (.clk(in_3), .D(in_4[1]), .Q(B[1]));  // open: Qn, preset, en, reset
  D_Flip_Flop d_ff_16 (.clk(in_3), .D(in_4[0]), .Q(B[0]));  // open: Qn, preset, en, reset
  // Probe on B
endmodule
