// Logisim project eduardo_perez_fraguela_PD0.circ as structural Verilog: 4 circuits, main circuit 4 bit adder
module _4_bit_adder (
  input  B3,
  input  B2,
  input  B1,
  input  B0,
  input  A3,
  input  A2,
  input  A1,
  input  A0,
  input  c_in,
  output C_OUT,
  output S3,
  output S2,
  output S1,
  output S0
);

  wire fa_2_c_out, fa_3_c_out, fa_4_c_out, xor_1_out, xor_2_out, xor_3_out, xor_4_out;

  FA fa_1 (.a(A3), .b(xor_1_out), .c_in(fa_3_c_out), .c_out(C_OUT), .s(S3));
  xor xor_1 (xor_1_out, B3, c_in);
  FA fa_2 (.a(A1), .b(xor_2_out), .c_in(fa_4_c_out), .c_out(fa_2_c_out), .s(S1));
  FA fa_3 (.a(A2), .b(xor_3_out), .c_in(fa_2_c_out), .c_out(fa_3_c_out), .s(S2));
  xor xor_2 (xor_2_out, B1, c_in);
  xor xor_3 (xor_3_out, B2, c_in);
  FA fa_4 (.a(A0), .b(xor_4_out), .c_in(c_in), .c_out(fa_4_c_out), .s(S0));
  xor xor_4 (xor_4_out, B0, c_in);
endmodule

module ejercicio (
  input  in_1,
  input  in_2,
  input  in_3,
  input  in_4,
  input  in_5,
  input  in_6,
  input  in_7,
  input  in_8,
  input  SELECT,
  output X3,
  output X2,
  output X1,
  output X0
);

  wire [3:0] A_B, A_B_1;

  // Probe on A_B[0]
  // Probe on A_B[1]
  // Probe on A_B[2]
  // Probe on A_B[3]
  // Probe on A_B_1[3]
  // Probe on A_B_1[2]
  // Probe on A_B_1[1]
  // Probe on A_B_1[0]
  _4_bit_adder u_4_bit_adder_1 (
    .c_in(1'b0), .A3(in_1), .A2(in_2), .A1(in_3), .A0(in_4), .B3(in_5), .B2(in_6), .B1(in_7), .B0(in_8),
    .S3(A_B[0]), .S2(A_B[1]), .S1(A_B[2]), .S0(A_B[3]));  // open: C_OUT
  _4_bit_adder u_4_bit_adder_2 (
    .c_in(1'b1), .A3(A_B[0]), .A2(A_B[1]), .A1(A_B[2]), .A0(A_B[3]), .B3(1'b0), .B2(1'b0), .B1(1'b0),
    .B0(1'b1), .S3(A_B_1[3]), .S2(A_B_1[2]), .S1(A_B_1[1]), .S0(A_B_1[0]));  // open: C_OUT
  Multiplexer #(.width(4), .disabled(0), .enable("false")) multiplexer_1 (
    .in0(A_B), .in1(A_B_1), .out({X3, X2, X1, X0}), .sel(SELECT));
endmodule

module FA (
  input  a,
  input  b,
  input  c_in,
  output c_out,
  output s
);

  wire and_1_out, and_2_out, or_1_out;

  and and_1 (and_1_out, a, b);
  or or_1 (or_1_out, a, b);
  or or_2 (c_out, and_1_out, and_2_out);
  and and_2 (and_2_out, or_1_out, c_in);
  xor xor_1 (s, a, b, c_in);
endmodule

module CIRCUITOFINAL (
  input  [3:0] in_1,
  input  [3:0] in_2,
  input  in_3,
  output [3:0] out_4
);

  ejercicio ejercicio_1 (
    .in_1(in_1[3]), .in_2(in_1[2]), .in_3(in_1[1]), .in_4(in_1[0]), .in_5(in_2[3]), .in_6(in_2[2]),
    .in_7(in_2[1]), .in_8(in_2[0]), .X3(out_4[3]), .X2(out_4[2]), .X1(out_4[1]), .X0(out_4[0]), .SELECT(in_3));
endmodule
