// Logisim project eduardo_perez_fraguela_PD1.circ as structural Verilog: 1 circuit, main circuit main
module main (
  input  a3,
  input  a2,
  input  a1,
  input  a0,
  input  b3,
  input  b2,
  input  b1,
  input  b0,
  output s0,
  output s1,
  output s2,
  output s3,
  output s4,
  output s0_2,
  output s1_2,
  output s2_2,
  output s3_2,
  output s4_2,
  output [4:0] out_19
);

  wire comparator_1_gt, comparator_2_lt, or_1_out;
  wire [4:0] not_5_out;

  not not_1 (not_5_out[3], 1'b0);
  not not_2 (not_5_out[4], 1'b0);
  not not_3 (not_5_out[1], 1'b0);
  not not_4 (not_5_out[2], 1'b1);
  Adder #(.width(5)) adder_1 (
    .a({b3, b2, b1, b0, 1'b0}), .b(not_5_out), .out({s4_2, s3_2, s2_2, s1_2, s0_2}), .cin(1'b1));  // open: cout
  not not_5 (not_5_out[0], 1'b0);
  Adder #(.width(5)) adder_2 (
    .a({1'b0, a3, a2, a1, a0}), .b(5'b00011), .out({s4, s3, s2, s1, s0}), .cin(1'b0));  // open: cout
  Multiplexer #(.width(5), .disabled(0), .enable("false")) multiplexer_1 (
    .in0({s4, s3, s2, s1, s0}), .in1({s4_2, s3_2, s2_2, s1_2, s0_2}), .out(out_19), .sel(or_1_out));
  Comparator #(.width(5), .mode("unsigned")) comparator_1 (
    .a({1'b0, a3, a2, a1, a0}), .b(5'b00011), .gt(comparator_1_gt));  // open: eq, lt
  Comparator #(.width(5), .mode("unsigned")) comparator_2 (
    .a({b3, b2, b1, b0, 1'b0}), .b(5'b00100), .lt(comparator_2_lt));  // open: gt, eq
  or or_1 (or_1_out, comparator_2_lt, comparator_1_gt);

  // Other names for the same wires on the sheet: B[4:1] = {b3, b2, b1, b0}
endmodule
