// Logisim project perez_fraguela_eduardo_PD2.circ as structural Verilog: 1 circuit, main circuit main
module main (
  input  [3:0] in_1,
  input  in_2
);

  wire CICLO_7, CLK, comparator_1_eq, comparator_3_gt, INICIO, or_1_out;
  wire [2:0] RESULTADO, Y;
  wire [3:0] A, CONT;

  Clock clock_1 (.out(CLK));
  Register #(.width(4)) register_1 (.D(in_1), .Q(A), .clk(CLK), .clr(in_2));  // open: en
  // Probe on A
  // Probe on in_1
  // Probe on A
  Counter #(.width(4), .max('hf)) counter_1 (.Q(CONT), .clk(CLK), .clr(in_2));  // open: load, D, count, carry
  Multiplexer #(.width(3), .disabled(0), .enable("false")) multiplexer_1 (
    .in0(RESULTADO), .out(Y), .sel(comparator_1_eq));  // open: in1
  Comparator #(.width(4), .mode("unsigned")) comparator_1 (
    .a(CONT), .b(4'b1000), .eq(comparator_1_eq));  // open: gt, lt
  Comparator #(.width(4), .mode("unsigned")) comparator_2 (.a(4'b0000), .b(CONT), .eq(INICIO));  // open: gt, lt
  Comparator #(.width(4), .mode("unsigned")) comparator_3 (
    .a({in_1[3:1], A[0]}), .b({A[3:1], in_1[0]}), .gt(comparator_3_gt));  // open: eq, lt
  // Probe on Y
  or or_1 (or_1_out, comparator_3_gt, INICIO, CICLO_7);
  Counter #(.width(3), .max('h7)) counter_2 (
    .count(or_1_out), .Q(RESULTADO), .clk(CLK), .clr(in_2));  // open: load, D, carry
  Comparator #(.width(4), .mode("unsigned")) comparator_4 (.a(4'b0111), .b(CONT), .eq(CICLO_7));  // open: gt, lt

  // Other names for the same wires on the sheet: X[3:0] = in_1; RESET = in_2
endmodule
